# Fritzing sketch Cerebro del niño (saved by Fritzing 0.9.3b)
breadboards: 2

parts:
  Componente1 = Arduino Nano (Rev3.0) (ICSP)
  Componente2 = Arduino Nano (Rev3.0) (ICSP)
  Raspberry_Pi_1 = Raspberry Pi 3 [part_number=RPI-3-V1.2]
  R1 = Resistor [tolerance=±5% resistance=220 package="2010 [SMD]"]
  R2 = Resistor [tolerance=±5% resistance=220 package="2010 [SMD]"]
  U1 = LM2596-Step-Down-Converter [package=THT]

nets:
  GND: Componente1.GND, Componente2.GND, Raspberry_Pi_1.GND, U1.pin4
  VIN: Componente1.VIN, Componente2.VIN, U1.pin3
  N1: Componente1.A5, Componente2.A5, Raspberry_Pi_1.GPIO3, R2.Pin_0
  N2: Componente1.A4, Componente2.A4, Raspberry_Pi_1.GPIO2, R1.Pin_0

custom parts:
  LM2596-Step-Down-Converter: A dummy, proxy, ersatz, stand-in part for whatever you want. With 4 pins on a 100 mil inline pin header footprint.
