# Fritzing sketch walliupdate (saved by Fritzing 0.9.3b)
circuit board: 10.46cm x 6.19cm
breadboards: 1

parts:
  SDA = Resistor [tolerance=±5% resistance=220 package=THT]
  SCL = Resistor [tolerance=±5% resistance=220 package=THT]
  5V_OUTLET = female pin header, 9 pins [form="♀ (female)"]
  SDA_OUTLET = female pin header, 9 pins [form="♀ (female)"]
  RPI1GND5 = female pin header, 10 pins [form="♀ (female)"]
  RPI1GND6 = female pin header, 1 pin [form="♀ (female)"]
  MIZQ2 = female pin header, 4 pins [form="♀ (female)"]
  RPI1GND3 = female pin header, 7 pins [form="♀ (female)"]
  MIZQ1 = female pin header, 4 pins [form="♀ (female)"]
  RPI1GND4 = female pin header, 7 pins [form="♀ (female)"]
  MDER = female pin header, 4 pins [form="♀ (female)"]
  RPI1GND = female pin header, 1 pin [form="♀ (female)"]
  RPI1GND1 = female pin header, 10 pins [form="♀ (female)"]
  RPI1GND2 = female pin header, 1 pin [form="♀ (female)"]
  MIZQ = female pin header, 4 pins [form="♀ (female)"]
  RPI_i2c = female pin header, 2 pins [form="♀ (female)"]
  GND_OUTLET = female pin header, 9 pins [form="♀ (female)"]
  5V_INPUT = Power Jack [package=power_jack_slot]
  MIZQ_NANO = Arduino Nano (Rev3.0)
  MDER_NANO = Arduino Nano (Rev3.0)
  X1 = USB Connectors [package=usb-a-h]
  SCL_OUTLET = female pin header, 9 pins [form="♀ (female)"]

nets:
  N1: SDA.Pin_0, RPI_i2c.pin1, MIZQ_NANO.A4, MDER_NANO.A4
  VIN: SDA.Pin_1, SCL.Pin_1, 5V_OUTLET.pin1, 5V_OUTLET.pin2, 5V_OUTLET.pin3, 5V_OUTLET.pin4, 5V_OUTLET.pin5, 5V_OUTLET.pin6, 5V_OUTLET.pin7, 5V_OUTLET.pin8, 5V_OUTLET.pin9, SDA_OUTLET.pin1, SDA_OUTLET.pin2, SDA_OUTLET.pin3, SDA_OUTLET.pin4, SDA_OUTLET.pin5, SDA_OUTLET.pin6, SDA_OUTLET.pin7, SDA_OUTLET.pin8, SDA_OUTLET.pin9, 5V_INPUT.PWR, MIZQ_NANO.VIN, MDER_NANO.VIN, X1.VBUS
  N2: SCL.Pin_0, RPI_i2c.pin2, MIZQ_NANO.A5, MDER_NANO.A5, SCL_OUTLET.pin1, SCL_OUTLET.pin2, SCL_OUTLET.pin3, SCL_OUTLET.pin4, SCL_OUTLET.pin5, SCL_OUTLET.pin6, SCL_OUTLET.pin7, SCL_OUTLET.pin8, SCL_OUTLET.pin9
  N3: RPI1GND5.pin1, MDER_NANO.D1/TX
  N4: RPI1GND5.pin2, MDER_NANO.D0/RX
  N5: RPI1GND5.pin3, MIZQ2.pin4, MDER_NANO.RESET
  GND: RPI1GND5.pin4, RPI1GND.pin1, RPI1GND1.pin7, GND_OUTLET.pin1, GND_OUTLET.pin2, GND_OUTLET.pin3, GND_OUTLET.pin4, GND_OUTLET.pin5, GND_OUTLET.pin6, GND_OUTLET.pin7, GND_OUTLET.pin8, GND_OUTLET.pin9, 5V_INPUT.GND, MIZQ_NANO.GND, MDER_NANO.GND
  N6: RPI1GND5.pin5, MDER_NANO.D2
  N7: RPI1GND5.pin6, MDER_NANO.D3
  N8: RPI1GND5.pin7, MDER_NANO.D4
  N9: RPI1GND5.pin8, MDER_NANO.D5
  N10: RPI1GND5.pin9, MDER_NANO.D6
  N11: RPI1GND5.pin10, MDER_NANO.D7
  N12: RPI1GND6.pin1, MDER_NANO.D12/MISO
  N13: MIZQ2.pin1, MDER_NANO.A6
  N14: MIZQ2.pin2, MDER_NANO.A7
  N15: MIZQ2.pin3, MDER_NANO.5V
  N16: RPI1GND3.pin1, MIZQ_NANO.D13/SCK
  N17: RPI1GND3.pin2, MIZQ_NANO.3V3
  N18: RPI1GND3.pin3, MIZQ_NANO.AREF
  N19: RPI1GND3.pin4, MIZQ_NANO.A0
  N20: RPI1GND3.pin5, MIZQ_NANO.A1
  N21: RPI1GND3.pin6, MIZQ_NANO.A2
  N22: RPI1GND3.pin7, MIZQ_NANO.A3
  N23: MIZQ1.pin1, RPI1GND1.pin8, MIZQ_NANO.RESET
  N24: MIZQ1.pin2, MIZQ_NANO.5V
  N25: MIZQ1.pin3, MIZQ_NANO.A7
  N26: MIZQ1.pin4, MIZQ_NANO.A6
  N27: RPI1GND4.pin1, MDER_NANO.A3
  N28: RPI1GND4.pin2, MDER_NANO.A2
  N29: RPI1GND4.pin3, MDER_NANO.A1
  N30: RPI1GND4.pin4, MDER_NANO.A0
  N31: RPI1GND4.pin5, MDER_NANO.AREF
  N32: RPI1GND4.pin6, MDER_NANO.3V3
  N33: RPI1GND4.pin7, MDER_NANO.D13/SCK
  N34: MDER.pin1, MDER_NANO.D11/MOSI
  N35: MDER.pin2, MDER_NANO.D10
  N36: MDER.pin3, MDER_NANO.D9
  N37: MDER.pin4, MDER_NANO.D8
  N38: RPI1GND1.pin1, MIZQ_NANO.D7
  N39: RPI1GND1.pin2, MIZQ_NANO.D6
  N40: RPI1GND1.pin3, MIZQ_NANO.D5
  N41: RPI1GND1.pin4, MIZQ_NANO.D4
  N42: RPI1GND1.pin5, MIZQ_NANO.D3
  N43: RPI1GND1.pin6, MIZQ_NANO.D2
  N44: RPI1GND1.pin9, MIZQ_NANO.D0/RX
  N45: RPI1GND1.pin10, MIZQ_NANO.D1/TX
  N46: RPI1GND2.pin1, MIZQ_NANO.D12/MISO
  N47: MIZQ.pin1, MIZQ_NANO.D8
  N48: MIZQ.pin2, MIZQ_NANO.D9
  N49: MIZQ.pin3, MIZQ_NANO.D10
  N50: MIZQ.pin4, MIZQ_NANO.D11/MOSI
  N51: 5V_INPUT.GNDBREAK, X1.GND

notes:
  WALK-E
